// Logisim project simd.circ as structural Verilog: 9 circuits, main circuit main
module main (
  output [7:0] out_1,
  output [7:0] out_2,
  output [7:0] out_3,
  output [7:0] out_4,
  output [7:0] out_5,
  output [7:0] out_6,
  output [7:0] out_7,
  output [7:0] out_8,
  output [7:0] out_9,
  output [7:0] out_10
);

  wire and_1_out, clear, clk, ehBranch, zero;
  wire [6:0] ctrlScalar, ctrlVET;
  wire [7:0] adder_1_out, multiplexer_1_out, register_1_q, rom_1_data, saguiscalar_1_saidarb;

  Adder adder_1 (.a(register_1_q), .b(8'h1), .out(adder_1_out), .cin(1'b0));  // open: cout
  Multiplexer #(.width(8)) multiplexer_1 (
    .in0(adder_1_out), .in1(saguiscalar_1_saidarb), .out(multiplexer_1_out), .sel(and_1_out));
  and and_1 (and_1_out, zero, ehBranch);
  Clock clock_1 (.out(clk));
  Register register_1 (.D(multiplexer_1_out), .en(1'b1), .clk(clk), .Q(register_1_q), .clr(clear));
  Button button_1 (.out(clear));
  ROM rom_1 (.addr(register_1_q), .data(rom_1_data));
  MemCtrl memctrl_1 (.branch(ehBranch), .ctrlVetorial(ctrlVET), .ctrlScalar(ctrlScalar), .Entrada(rom_1_data[7:4]));
  saguiVet saguivet_1 (
    .out_6(out_1), .out_7(out_2), .controle(ctrlVET), .clk(clk), .Ra(rom_1_data[3:2]), .Rb(rom_1_data[1:0]),
    .clear(clear));
  saguiVet saguivet_2 (
    .out_6(out_3), .out_7(out_4), .controle(ctrlVET), .clk(clk), .Ra(rom_1_data[3:2]), .Rb(rom_1_data[1:0]),
    .clear(clear));
  saguiVet saguivet_3 (
    .out_6(out_5), .out_7(out_6), .controle(ctrlVET), .clk(clk), .Ra(rom_1_data[3:2]), .Rb(rom_1_data[1:0]),
    .clear(clear));
  saguiVet saguivet_4 (
    .out_6(out_7), .out_7(out_8), .controle(ctrlVET), .clk(clk), .Ra(rom_1_data[3:2]), .Rb(rom_1_data[1:0]),
    .clear(clear));
  saguiScalar saguiscalar_1 (
    .out_6(out_9), .out_7(out_10), .SaidaRB(saguiscalar_1_saidarb), .ehZero(zero), .controle(ctrlScalar),
    .clk(clk), .Ra(rom_1_data[3:2]), .Rb(rom_1_data[1:0]), .clear(clear));

  // Notes on the sheet:
  //   contents of rom_1 (hex, n*v repeats v):
  //   b3 91 8f cc 9c a1 d3 f3 e3 33 11 f 4c 1c 21 53 63 13 7 b 21 56 74 43 5f 5f 7c
endmodule

module MemCtrl (
  input  [3:0] Entrada,
  output [6:0] ctrlScalar,
  output [6:0] ctrlVetorial,
  output branch
);

  wire and_1_out;
  wire [6:0] demultiplexer_1_out0, rom_1_data;

  and and_1 (and_1_out, Entrada[2], Entrada[1], Entrada[0]);
  and and_2 (branch, ~Entrada[3], and_1_out);  // AND_Gate
  ROM #(.addrWidth(3), .dataWidth(7)) rom_1 (.addr(Entrada[2:0]), .data(rom_1_data));
  Demultiplexer #(.width(7)) demultiplexer_1 (
    .out0(demultiplexer_1_out0), .out1(ctrlVetorial), .in(rom_1_data), .sel(Entrada[3]));
  Multiplexer #(.width(7)) multiplexer_1 (.in0(demultiplexer_1_out0), .in1({7{1'b0}}), .out(ctrlScalar), .sel(branch));

  // Notes on the sheet:
  //   contents of rom_1 (hex, n*v repeats v):
  //   26 46 3c 3d 30 31 32 33
endmodule

module saguiScalar (
  input  clk,
  input  clear,
  input  [6:0] controle,
  input  [1:0] Ra,
  input  [1:0] Rb,
  output [7:0] out_6,
  output [7:0] out_7,
  output ehZero,
  output [7:0] SaidaRB
);

  wire [1:0] multiplexer_1_out;
  wire [7:0] bancoregs_1_saidaa, bit_extender_1_out, multiplexer_2_out, multiplexer_3_out;

  assign bit_extender_1_out = {{4{Ra[1]}}, {Ra, Rb}};  // Bit_Extender bit_extender_1
  Multiplexer #(.width(2)) multiplexer_1 (.in0(Ra), .in1(2'b00), .out(multiplexer_1_out), .sel(controle[3]));
  bancoRegs bancoregs_1 (
    .saidaA(bancoregs_1_saidaa), .saidaB(SaidaRB), .clk(clk), .rst(clear), .ra(multiplexer_1_out), .rb(Rb),
    .dadosEscrita(multiplexer_3_out), .write(controle[5]));
  Multiplexer #(.width(8)) multiplexer_2 (
    .in0(SaidaRB), .in1(bit_extender_1_out), .out(multiplexer_2_out), .sel(controle[3]));
  ULAscalar ulascalar_1 (
    .ehZero(ehZero), .saida(out_6), .A(bancoregs_1_saidaa), .B(multiplexer_2_out), .Op(controle[2:0]));
  RAM #(.asyncread("true"), .clearpin("true")) ram_1 (
    .addr(out_6), .we(controle[6]), .oe(1'b1), .clk(clk), .din(bancoregs_1_saidaa), .dout(out_7));  // open: clr
  Multiplexer #(.width(8)) multiplexer_3 (.in0(out_7), .in1(out_6), .out(multiplexer_3_out), .sel(controle[4]));

  // Other names for the same wires on the sheet: cls = clear; Imediato = controle[3]; saidaULA = controle[4];
  //   writeReg = controle[5]; writeMEM = controle[6]; opULA[2:0] = controle[2:0]
endmodule

module ULAscalar (
  input  [7:0] A,
  input  [2:0] Op,
  input  [7:0] B,
  output ehZero,
  output [7:0] saida
);

  wire [7:0] adder_1_out, adder_2_out, and_1_out, movh_1_saida, movl_1_saida, not_1_out, or_1_out;

  nor nor_1 (ehZero, A[0], A[1], A[2], A[3], A[4], A[5], A[6], A[7]);
  assign not_1_out = ~B;  // NOT_Gate not_1, 8 bits wide
  Adder adder_1 (.a(A), .b(B), .out(adder_1_out), .cin(1'b0));  // open: cout
  Adder adder_2 (.a(A), .b(not_1_out), .out(adder_2_out), .cin(1'b1));  // open: cout
  assign and_1_out = A & B;  // AND_Gate and_1, 8 bits wide
  assign or_1_out = A | B;  // OR_Gate or_1, 8 bits wide
  movH movh_1 (.saida(movh_1_saida), .A(A), .B(B));
  movl movl_1 (.saida(movl_1_saida), .A(A), .B(B));
  Multiplexer #(.select(3), .width(8)) multiplexer_1 (
    .in0(adder_1_out), .in1(adder_2_out), .in2(and_1_out), .in3(or_1_out), .in4(movh_1_saida),
    .in5(movl_1_saida), .in6(B), .in7({8{1'b0}}), .out(saida), .sel(Op));
endmodule

module saguiVet (
  input  clk,
  input  clear,
  input  [6:0] controle,
  input  [1:0] Ra,
  input  [1:0] Rb,
  output [7:0] out_6,
  output [7:0] out_7
);

  wire [1:0] multiplexer_1_out;
  wire [7:0] bancoregs_1_saidaa, bancoregs_1_saidab, bit_extender_1_out, multiplexer_2_out, multiplexer_3_out;

  assign bit_extender_1_out = {{4{Ra[1]}}, {Ra, Rb}};  // Bit_Extender bit_extender_1
  Multiplexer #(.width(2)) multiplexer_1 (.in0(Ra), .in1(2'b00), .out(multiplexer_1_out), .sel(controle[3]));
  bancoRegs bancoregs_1 (
    .saidaA(bancoregs_1_saidaa), .saidaB(bancoregs_1_saidab), .clk(clk), .rst(clear), .ra(multiplexer_1_out),
    .rb(Rb), .dadosEscrita(multiplexer_3_out), .write(controle[5]));
  Multiplexer #(.width(8)) multiplexer_2 (
    .in0(bancoregs_1_saidab), .in1(bit_extender_1_out), .out(multiplexer_2_out), .sel(controle[3]));
  ULAvet ulavet_1 (.saida(out_6), .A(bancoregs_1_saidaa), .B(multiplexer_2_out), .Op(controle[2:0]));
  RAM #(.asyncread("true"), .clearpin("true")) ram_1 (
    .addr(out_6), .we(controle[6]), .oe(1'b1), .clk(clk), .din(bancoregs_1_saidaa), .dout(out_7));  // open: clr
  Multiplexer #(.width(8)) multiplexer_3 (.in0(out_7), .in1(out_6), .out(multiplexer_3_out), .sel(controle[4]));

  // Other names for the same wires on the sheet: cls = clear; Imediato = controle[3]; saidaULA = controle[4];
  //   writeReg = controle[5]; writeMEM = controle[6]; opULA[2:0] = controle[2:0]
endmodule

module ULAvet (
  input  [7:0] A,
  input  [2:0] Op,
  input  [7:0] B,
  output [7:0] saida
);

  wire [7:0] adder_1_out, adder_2_out, and_1_out, movh_1_saida, movl_1_saida, not_1_out, or_1_out;

  assign not_1_out = ~B;  // NOT_Gate not_1, 8 bits wide
  Adder adder_1 (.a(A), .b(B), .out(adder_1_out), .cin(1'b0));  // open: cout
  Adder adder_2 (.a(A), .b(not_1_out), .out(adder_2_out), .cin(1'b1));  // open: cout
  assign and_1_out = A & B;  // AND_Gate and_1, 8 bits wide
  assign or_1_out = A | B;  // OR_Gate or_1, 8 bits wide
  movH movh_1 (.saida(movh_1_saida), .A(A), .B(B));
  movl movl_1 (.saida(movl_1_saida), .A(A), .B(B));
  Multiplexer #(.select(3), .width(8)) multiplexer_1 (
    .in0(adder_1_out), .in1(adder_2_out), .in2(and_1_out), .in3(or_1_out), .in4(movh_1_saida),
    .in5(movl_1_saida), .in6(B), .in7({8{1'b0}}), .out(saida), .sel(Op));
endmodule

module bancoRegs (
  input  write,
  input  [7:0] dadosEscrita,
  input  clk,
  input  rst,
  input  [1:0] ra,
  input  [1:0] rb,
  output [7:0] saidaA,
  output [7:0] saidaB
);

  wire w1, w2, w3, w4;
  wire [7:0] demultiplexer_1_out0, demultiplexer_1_out1, demultiplexer_1_out2, demultiplexer_1_out3, R1_q,
       R2_q, R3_q, R4_q;

  Register R1 (.D(demultiplexer_1_out0), .en(w1), .clk(clk), .Q(R1_q), .clr(rst));
  Multiplexer #(.select(2), .width(8)) multiplexer_1 (
    .in0(R1_q), .in1(R2_q), .in2(R3_q), .in3(R4_q), .out(saidaA), .sel(ra));
  Multiplexer #(.select(2), .width(8)) multiplexer_2 (
    .in0(R1_q), .in1(R2_q), .in2(R3_q), .in3(R4_q), .out(saidaB), .sel(rb));
  Demultiplexer #(.select(2), .width(8)) demultiplexer_1 (
    .out0(demultiplexer_1_out0), .out1(demultiplexer_1_out1), .out2(demultiplexer_1_out2),
    .out3(demultiplexer_1_out3), .in(dadosEscrita), .sel(ra));
  Register R2 (.D(demultiplexer_1_out1), .en(w2), .clk(clk), .Q(R2_q), .clr(rst));
  Demultiplexer #(.select(2)) demultiplexer_2 (.out0(w1), .out1(w2), .out2(w3), .out3(w4), .in(write), .sel(ra));
  Register R3 (.D(demultiplexer_1_out2), .en(w3), .clk(clk), .Q(R3_q), .clr(rst));
  Register R4 (.D(demultiplexer_1_out3), .en(w4), .clk(clk), .Q(R4_q), .clr(rst));
endmodule

module movH (
  input  [7:0] A,
  input  [7:0] B,
  output [7:0] saida
);


  assign B[6:4] = {3{B[7]}};
  assign saida = {B[3:0], A[3:0]};
  // also tied to GND on the sheet: {A[4], A[5], A[6], A[7], B[7]}
endmodule

module movl (
  input  [7:0] A,
  input  [7:0] B,
  output [7:0] saida
);


  assign A[2:0] = {3{A[3]}};
  assign B[6:4] = {3{B[7]}};
  assign saida = {A[7:4], B[3:0]};
  // also tied to GND on the sheet: {A[3], B[7]}
endmodule
