// Logisim project sagui.circ as structural Verilog: 6 circuits, main circuit main
module main (
  output [7:0] out_1,
  output [7:0] out_2,
  output [7:0] out_3
);

  wire and_1_out, clk, cls, ehZero, immOUregB, JouZ, jump, memcontrole_1_writereg, memOUreg,
       multiplexer_2_out, multiplexer_4_out, regZero, writeMEM;
  wire [1:0] multiplexer_5_out;
  wire [3:0] opULA;
  wire [7:0] adder_1_out, bancoregs_1_saidaa, bancoregs_1_saidab, bit_extender_1_out, multiplexer_1_out,
       multiplexer_3_out, multiplexer_6_out, multiplexer_7_out, register_1_q, rom_1_data;

  Multiplexer #(.width(8)) multiplexer_1 (
    .in0(8'h1), .in1(bit_extender_1_out), .out(multiplexer_1_out), .sel(multiplexer_2_out));
  Multiplexer multiplexer_2 (.in0(jump), .in1(ehZero), .out(multiplexer_2_out), .sel(JouZ));
  Adder adder_1 (.a(register_1_q), .b(multiplexer_1_out), .out(adder_1_out), .cin(1'b0));  // open: cout
  Multiplexer #(.width(8)) multiplexer_3 (
    .in0(adder_1_out), .in1(bancoregs_1_saidab), .out(multiplexer_3_out), .sel(and_1_out));
  and and_1 (and_1_out, ~immOUregB, multiplexer_4_out, jump);  // AND_Gate
  Register register_1 (.D(multiplexer_3_out), .en(1'b1), .clk(clk), .Q(register_1_q), .clr(cls));
  Multiplexer multiplexer_4 (.in0(ehZero), .in1(1'b1), .out(multiplexer_4_out), .sel(regZero));
  Clock clock_1 (.out(clk));
  ROM rom_1 (.addr(register_1_q), .data(rom_1_data));
  Button button_1 (.out(cls));
  MemControle memcontrole_1 (
    .immOUregb(immOUregB), .opULA(opULA), .regZero(regZero), .memOUreg(memOUreg), .Jump(jump),
    .writeMEM(writeMEM), .writeREG(memcontrole_1_writereg), .JouZ(JouZ), .Entrada(rom_1_data[7:4]));
  Multiplexer #(.width(2)) multiplexer_5 (.in0(rom_1_data[3:2]), .in1(2'b00), .out(multiplexer_5_out), .sel(regZero));
  assign bit_extender_1_out = {{4{rom_1_data[3]}}, rom_1_data[3:0]};  // Bit_Extender bit_extender_1
  bancoRegs bancoregs_1 (
    .saidaA(bancoregs_1_saidaa), .saidaB(bancoregs_1_saidab), .clk(clk), .rst(cls), .ra(multiplexer_5_out),
    .rb(rom_1_data[1:0]), .dadosEscrita(multiplexer_7_out), .write(memcontrole_1_writereg));
  Multiplexer #(.width(8)) multiplexer_6 (
    .in0(bancoregs_1_saidab), .in1(bit_extender_1_out), .out(multiplexer_6_out), .sel(immOUregB));
  ULA ula_1 (.ehZero(ehZero), .saida(out_1), .A(bancoregs_1_saidaa), .B(multiplexer_6_out), .Op(opULA));
  RAM ram_1 (.addr(out_1), .we(writeMEM), .oe(1'b1), .clk(clk), .din(bancoregs_1_saidaa), .dout(out_3));
  Multiplexer #(.width(8)) multiplexer_7 (.in0(out_3), .in1(out_1), .out(multiplexer_7_out), .sel(memOUreg));

  assign out_2 = out_1;

  // Notes on the sheet:
  //   contents of rom_1 (hex, n*v repeats v):
  //   8c 64 63 71 94 54 48 a6 b8 81 70 6e ec f8 c8 d6 b aa 3e 10*0 30 0 0 1d a0 23
endmodule

module MemControle (
  input  [3:0] Entrada,
  output [3:0] opULA,
  output immOUregb,
  output regZero,
  output memOUreg,
  output Jump,
  output writeMEM,
  output writeREG,
  output JouZ
);

  ROM #(.addrWidth(4), .dataWidth(11)) rom_1 (
    .addr(Entrada), .data({JouZ, writeREG, writeMEM, Jump, memOUreg, regZero, immOUregb, opULA}));

  // Notes on the sheet:
  //   contents of rom_1 (hex, n*v repeats v):
  //   480 430 a0 90 209 109 249 277 278 240 241 242 243 244 245 246
endmodule

module ULA (
  input  [7:0] A,
  input  [3:0] Op,
  input  [7:0] B,
  output ehZero,
  output [7:0] saida
);

  wire or_1_out;
  wire [7:0] adder_1_out, adder_2_out, and_1_out, movh_1_saida, movl_1_saida, multiplexer_1_out,
       multiplexer_2_out, not_1_out, or_2_out, shifter_1_out, shifter_2_out;

  nor nor_1 (ehZero, A[0], A[1], A[2], A[3], A[4], A[5], A[6], A[7]);
  or or_1 (or_1_out, B[7], B[6], B[5], B[4], B[3]);
  Adder adder_1 (.a(A), .b(B), .out(adder_1_out), .cin(1'b0));  // open: cout
  Adder adder_2 (.a(A), .b(not_1_out), .out(adder_2_out), .cin(1'b1));  // open: cout
  assign and_1_out = A & B;  // AND_Gate and_1, 8 bits wide
  assign or_2_out = A | B;  // OR_Gate or_2, 8 bits wide
  assign not_1_out = ~B;  // NOT_Gate not_1, 8 bits wide
  Shifter shifter_1 (.in(A), .\dist (B[2:0]), .out(shifter_1_out));
  Shifter #(.shift("lr")) shifter_2 (.in(A), .\dist (B[2:0]), .out(shifter_2_out));
  Multiplexer #(.width(8)) multiplexer_1 (
    .in0(shifter_1_out), .in1({8{1'b0}}), .out(multiplexer_1_out), .sel(or_1_out));
  Multiplexer #(.width(8)) multiplexer_2 (
    .in0(shifter_2_out), .in1({8{1'b0}}), .out(multiplexer_2_out), .sel(or_1_out));
  movH movh_1 (.saida(movh_1_saida), .A(A), .B(B));
  movl movl_1 (.saida(movl_1_saida), .A(A), .B(B));
  Multiplexer #(.select(4), .width(8)) multiplexer_3 (
    .in0(adder_1_out), .in1(adder_2_out), .in2(and_1_out), .in3(or_2_out), .in4(not_1_out),
    .in5(multiplexer_1_out), .in6(multiplexer_2_out), .in7(movh_1_saida), .in8(movl_1_saida), .in9(B),
    .in10({8{1'b0}}), .in11({8{1'b0}}), .in12({8{1'b0}}), .in13({8{1'b0}}), .in14({8{1'b0}}),
    .in15({8{1'b0}}), .out(saida), .sel(Op));
endmodule

module bancoRegs (
  input  write,
  input  [7:0] dadosEscrita,
  input  clk,
  input  rst,
  input  [1:0] ra,
  input  [1:0] rb,
  output [7:0] saidaA,
  output [7:0] saidaB
);

  wire w1, w2, w3, w4;
  wire [7:0] demultiplexer_1_out0, demultiplexer_1_out1, demultiplexer_1_out2, demultiplexer_1_out3,
       register_1_q, register_2_q, register_3_q, register_4_q;

  Register register_1 (.D(demultiplexer_1_out0), .en(w1), .clk(clk), .Q(register_1_q), .clr(rst));
  Multiplexer #(.select(2), .width(8)) multiplexer_1 (
    .in0(register_1_q), .in1(register_2_q), .in2(register_3_q), .in3(register_4_q), .out(saidaA), .sel(ra));
  Multiplexer #(.select(2), .width(8)) multiplexer_2 (
    .in0(register_1_q), .in1(register_2_q), .in2(register_3_q), .in3(register_4_q), .out(saidaB), .sel(rb));
  Demultiplexer #(.select(2), .width(8)) demultiplexer_1 (
    .out0(demultiplexer_1_out0), .out1(demultiplexer_1_out1), .out2(demultiplexer_1_out2),
    .out3(demultiplexer_1_out3), .in(dadosEscrita), .sel(ra));
  Register register_2 (.D(demultiplexer_1_out1), .en(w2), .clk(clk), .Q(register_2_q), .clr(rst));
  Demultiplexer #(.select(2)) demultiplexer_2 (.out0(w1), .out1(w2), .out2(w3), .out3(w4), .in(write), .sel(ra));
  Register register_3 (.D(demultiplexer_1_out2), .en(w3), .clk(clk), .Q(register_3_q), .clr(rst));
  Register register_4 (.D(demultiplexer_1_out3), .en(w4), .clk(clk), .Q(register_4_q), .clr(rst));
endmodule

module movH (
  input  [7:0] A,
  input  [7:0] B,
  output [7:0] saida
);


  assign B[6:4] = {3{B[7]}};
  assign saida = {B[3:0], A[3:0]};
  // also tied to GND on the sheet: {A[4], A[5], A[6], A[7], B[7]}
endmodule

module movl (
  input  [7:0] A,
  input  [7:0] B,
  output [7:0] saida
);


  assign A[2:0] = {3{A[3]}};
  assign B[6:4] = {3{B[7]}};
  assign saida = {A[7:4], B[3:0]};
  // also tied to GND on the sheet: {A[3], B[7]}
endmodule
